// Logisim project Hexa2022.circ as structural Verilog: 1 circuit, main circuit main
module main (
  input  _0,
  input  _1,
  input  _2,
  input  _3,
  input  _4,
  input  _5,
  input  _6,
  input  _7,
  input  _8,
  input  _9,
  input  _10,
  input  _11,
  input  _12,
  input  _13,
  input  _14,
  input  _15,
  input  _0_2,
  input  _1_2,
  input  _2_2,
  input  _3_2,
  input  _4_2,
  input  _5_2,
  input  _6_2,
  input  _7_2,
  input  _8_2,
  input  _9_2,
  input  _10_2,
  input  _11_2,
  input  _12_2,
  input  _13_2,
  input  _14_2,
  input  in_32,
  input  _15_2
);

  wire and_1_out, main_1_p17, main_2_p17, main_3_p2, main_4_p3, main_4_p4, main_5_p2, main_5_p3, main_5_p4,
       main_5_p5, main_5_p6, main_5_p7, main_5_p8, MUX_p4;

  // Conversor_Hexadecimal_main main_1: pin names not known; wires that end beside it: _0, _1, _2, _3, _4, _5, _6, _7, _8, _9, _10, _11, _12, _13, _14, _15, main_1_p17
  // Conversor_Hexadecimal_main main_2: pin names not known; wires that end beside it: _0_2, _1_2, _2_2, _3_2, _4_2, _5_2, _6_2, _7_2, _8_2, _9_2, _10_2, _11_2, _12_2, _13_2, _14_2, _15_2, main_2_p17
  // C2_main main_3: pin names not known; wires that end beside it: main_2_p17, main_3_p2
  // Mux_4bit_main MUX: pin names not known; wires that end beside it: main_2_p17, main_3_p2, in_32, MUX_p4
  // UnidArit4bits_main main_4: pin names not known; wires that end beside it: main_1_p17, MUX_p4, main_4_p3, main_4_p4
  and and_1 (and_1_out, main_4_p3, ~in_32);  // AND_Gate
  // _7_seg_main main_5: pin names not known; wires that end beside it: main_4_p4, main_5_p2, main_5_p3, main_5_p4, main_5_p5, main_5_p6, main_5_p7, main_5_p8
  _7_Segment_Display u_7_segment_display_1 (.b(and_1_out), .c(and_1_out));  // open: g, f, a, e, d, dp
  _7_Segment_Display u_7_segment_display_2 (
    .g(main_5_p8), .f(main_5_p7), .a(main_5_p2), .b(main_5_p3), .e(main_5_p6), .d(main_5_p5), .c(main_5_p4));  // open: dp
endmodule
